// Logisim project cpu.circ as structural Verilog: 1 circuit, main circuit main
module main (
  input  [15:0] in_1,
  input  [7:0] in_2,
  input  in_3,
  input  in_4,
  input  ADDR_TO_IP,
  input  IP_INC,
  input  IP_TO_ADDR,
  input  DATA_TO_ADDR_HI,
  input  ADDR_HI_TO_DATA,
  input  DATA_TO_ADDR_LO,
  input  ADDR_LO_TO_DATA,
  output [7:0] out_12,
  output [15:0] out_13,
  output [15:0] out_14
);

  wire and_1_out, and_2_out, CLK, or_1_out, or_2_out, RST;

  assign out_12 = in_3 ? in_2 : 8'bz;  // Controlled_Buffer controlled_buffer_1
  assign out_13[7:0] = DATA_TO_ADDR_LO ? out_12 : 8'bz;  // Controlled_Buffer controlled_buffer_2
  assign out_13[15:8] = DATA_TO_ADDR_HI ? out_12 : 8'bz;  // Controlled_Buffer controlled_buffer_3
  Button u_CLK (.out(CLK));
  Button u_RST (.out(RST));
  Counter #(.width(16), .max('hffff)) counter_1 (
    .load(ADDR_TO_IP), .D(out_13), .count(IP_INC), .Q(out_14), .clk(CLK), .clr(RST));  // open: carry
  assign out_13[7:0] = or_1_out ? out_14[7:0] : 8'bz;  // Controlled_Buffer controlled_buffer_4
  and and_1 (and_1_out, ADDR_TO_IP, DATA_TO_ADDR_HI);
  or or_1 (or_1_out, and_1_out, IP_TO_ADDR);
  or or_2 (or_2_out, IP_TO_ADDR, and_2_out);
  and and_2 (and_2_out, ADDR_TO_IP, DATA_TO_ADDR_LO);
  assign out_12 = ADDR_HI_TO_DATA ? out_13[15:8] : 8'bz;  // Controlled_Buffer controlled_buffer_5
  assign out_13 = in_4 ? in_1 : 16'bz;  // Controlled_Buffer controlled_buffer_6
  assign out_13[15:8] = or_2_out ? out_14[15:8] : 8'bz;  // Controlled_Buffer controlled_buffer_7
  assign out_12 = ADDR_LO_TO_DATA ? out_13[7:0] : 8'bz;  // Controlled_Buffer controlled_buffer_8

  // Notes on the sheet:
  //   Instruction Pointer
endmodule
